// Logisim project try.circ as structural Verilog: 1 circuit, main circuit main
module main (
  input  [3:0] in_1,
  input  in_2,
  output [15:0] out_3,
  output [15:0] out_4,
  output [11:0] out_5,
  output [15:0] out_6,
  output [15:0] out_7,
  output [15:0] out_8,
  output [15:0] out_9,
  output [15:0] out_10,
  output [15:0] out_11,
  output [15:0] out_12
);

  wire A0, A1, A2, ALUOp, ALUSrc, Branch, clock_1_out, Great_F, JAL, JALR, JR, Jump, Less_F, LUI, MemRead,
       MemtoReg, MemWrite, RegDst, RegWrite, Z_F;
  wire [0:0] Rs;
  wire [2:0] fun, main_3_rd_2, rom_1_data;
  wire [3:0] Imm6;
  wire [5:0] Imm12;
  wire [11:0] Imm, PC;
  wire [15:0] bit_extender_1_out, main_4_out_8, main_5_p7, Mem, multiplexer_1_out, Rs_pc;

  control_unit_main main_1 (
    .in_1(in_1), .\function (fun), .LUI(LUI), .R0(A0), .R1(A1), .R2(A2), .Branch(Branch), .Z_F(Z_F),
    .Great_F(Great_F), .Less_F(Less_F), .RegWrite(RegWrite), .RegDst(RegDst), .MemRead(MemRead),
    .MemtoReg(MemtoReg), .MemWrite(MemWrite), .ALUOp(ALUOp), .ALUSrc(ALUSrc), .Jump(Jump), .JR(JR),
    .JALR(JALR), .JAL(JAL), .Rt(Imm12[4:2]));
  PC_counter_main main_2 (
    .Imm12({A0, A1, Imm6, Imm12}), .Regester(Rs_pc), .Imm6({A0, A1, Imm6}), .JAL(JAL), .JR(JR), .JALR(JALR),
    .Branch(Branch), .out_11(out_5), .CLK(clock_1_out), .Reset(in_2), .J(Jump));
  Clock clock_1 (.out(clock_1_out));
  ROM #(.addrWidth(12), .dataWidth(16)) rom_1 (
    .addr(out_5), .data({A0, A1, Imm6, Imm12, Rs[0], rom_1_data}));  // open: sel
  RegFile_Decoder_main main_3 (
    .Rs({Imm12[1:0], Rs[0]}), .Rt(Imm12[4:2]), .Rd({Imm6[1:0], Imm12[5]}), .ALU(main_5_p7), .Mem(Mem),
    .PC(PC), .Imm(Imm), .Rd_2(main_3_rd_2), .data(out_3), .JALR(JALR), .LUI(LUI), .RegDst(JALR),
    .JALR_2(JALR), .MemtoReg(JALR));
  assign bit_extender_1_out = {{10{1'b0}}, {A0, A1, Imm6}};  // Bit_Extender bit_extender_1
  Regster_File_main main_4 (
    .Write_Register(main_3_rd_2), .Read_Register1({Imm12[1:0], Rs[0]}), .in_3(Imm12[4:2]), .in_4(out_3),
    .out_7(Rs_pc), .out_8(main_4_out_8), .in_5(RegWrite), .clock(clock_1_out), .out_9(out_4), .out_10(out_6),
    .out_11(out_7), .out_12(out_8), .out_13(out_9), .out_14(out_10), .out_15(out_11), .out_16(out_12));
  Multiplexer #(.width(16)) multiplexer_1 (
    .in0(main_4_out_8), .in1(bit_extender_1_out), .out(multiplexer_1_out), .sel(ALUSrc));  // open: en
  // FULL_ALU0__1__main main_5: pin names not known; wires that end beside it: A2, Less_F, A1, Great_F, A0, Z_F, main_5_p7, main_5_p7
  RAM #(.addrWidth(16), .dataWidth(16), .bus("separate")) ram_1 (
    .addr(main_5_p7), .din(main_4_out_8), .data(Mem), .str(MemWrite), .sel(1'b1), .clk(clock_1_out),
    .clr(MemRead));  // open: ld

  // Other names for the same wires on the sheet: Rs[2:1] = Imm12[1:0]; Rt[2:0] = Imm12[4:2];
  //   Rd[2:0] = {Imm6[1:0], Imm12[5]}; Imm12[11:6] = {A0, A1, Imm6}; Imm6[5:4] = {A0, A1}; op[3:0] = in_1;
  //   pc_t[11:0] = out_5; R0[15:0] = out_4; R1[15:0] = out_6; R2[15:0] = out_7; R3[15:0] = out_8; R4[15:0] = out_9;
  //   R5[15:0] = out_10; R6[15:0] = out_11; R7[15:0] = out_12

  // Notes on the sheet:
  //   contents of rom_1 (hex, n*v repeats v):
  //   a384 0 8354 0 35b 0 2040 0 2081 0 20c2 0 890a 0 1921 0 1520 0 14f2 0 4c02 0 1290 0 403b 0 3800 0
  //   b003 0 55c 0 1b68 0 4e9 0 2040 0 2285 0 22c6 0 4e0 0 3840 0 104e
endmodule
